// Logisim project maman12-q1.circ as structural Verilog: 1 circuit, main circuit main
module main (
  input  I0,
  input  I1,
  input  I2,
  input  I3,
  input  I4,
  input  I5,
  input  I6,
  input  I7,
  input  C,
  output O0,
  output O1,
  output O2,
  output O3,
  output O4,
  output O5,
  output O6,
  output O7
);

  wire and_1_out, and_3_out, and_4_out, and_5_out, and_6_out, and_7_out, and_8_out, and_9_out, and_10_out,
       and_11_out, and_12_out, and_14_out, not_1_out;

  not not_1 (not_1_out, C);
  and and_1 (and_1_out, I0, not_1_out);
  and and_2 (O0, C, I1);
  and and_3 (and_3_out, I1, not_1_out);
  and and_4 (and_4_out, C, I2);
  and and_5 (and_5_out, I2, not_1_out);
  and and_6 (and_6_out, C, I3);
  and and_7 (and_7_out, I3, not_1_out);
  and and_8 (and_8_out, I4, C);
  and and_9 (and_9_out, I4, not_1_out);
  and and_10 (and_10_out, I5, C);
  and and_11 (and_11_out, I5, not_1_out);
  and and_12 (and_12_out, I6, C);
  and and_13 (O7, I6, not_1_out);
  and and_14 (and_14_out, C, I7);
  or or_1 (O1, and_1_out, and_4_out);
  or or_2 (O2, and_3_out, and_6_out);
  or or_3 (O3, and_5_out, and_8_out);
  or or_4 (O4, and_7_out, and_10_out);
  or or_5 (O5, and_9_out, and_12_out);
  or or_6 (O6, and_11_out, and_14_out);
endmodule
